# Fritzing sketch sensor board (saved by Fritzing 0.9.3b)

parts:
  Part1 = Adafruit Feather M0 Adalogger [part_number="Adafruit #2796"]
  Part2 = Adafruit_BMP280
  Part3 = Adafruit FONA 808 Breakout [part_number="Adafruit #2542"]
  Part4 = Adafruit LSM9DS1 9DoF Breakout [part_number="Adafruit #3387"]

nets:
  N1: Part1.D1, Part3.RXD
  N2: Part1.D0, Part3.TXD
  GND: Part1.GND, Part2.GND, Part3.GND, Part3.Key, Part4.GND
  VIN: Part1.+3V3, Part2.VIN, Part3.Vio, Part4.VIN
  N3: Part1.D9, Part3.Reset
  N4: Part1.SCL, Part2.SCK/SCL, Part4.SCL
  N5: Part1.SDA, Part2.SDI/SDA, Part4.SDA

custom parts:
  Adafruit Feather M0 Adalogger: This is the Adafruit Feather M0 Adalogger - our take on an 'all-in-one' Cortex M0 datalogger (or data-reader) with built in USB and battery charging. Its an Adafruit Feather M0 with a microSD holder ready to rock! We have other boards in the Feather family, check'em out here At the Feather M0's heart is an ATSAMD21G18 ARM Cortex M0 processor, clocked at 48 MHz and at 3.3V logic, the same one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
  Adafruit_BMP280: Bosch has stepped up their game with their new BMP280 sensor, an environmental sensor with temperature, barometric pressure that is the next generation upgrade to the BMP085/BMP180/BMP183. This sensor is great for all sorts of weather sensing and can even be used in both I2C and SPI! This precision sensor from Bosch is the best low-cost, precision sensing solution for measuring barometric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
  Adafruit FONA 808 Breakout: Cellular + GPS tracking, all in one? Oh yes! Introducing Adafruit FONA 808 MiniGSM + GPS, an all-in-one cellular phone module with that lets you add location-tracking, voice, text, SMS and data to your project in an adorable little package.
  Adafruit LSM9DS1 9DoF Breakout: Add motion, direction and orientation sensing to your Arduino project with this all-in-one 9-DOF sensor. Inside the chip are three sensors, one is a classic 3-axis accelerometer, which can tell you which direction is down towards the Earth (by measuring gravity) or how fast the board is accelerating in 3D space. The other is a 3-axis magnetometer that can sense where the strongest magnetic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
