# Fritzing sketch sensor board2 (saved by Fritzing 0.9.3b)

parts:
  Part1 = Adafruit Feather 32u4 FONA [part_number="Adafruit #3027"]
  Part2 = Adafruit GPS FeatherWing [part_number="Adafruit #3133"]
  Part3 = Adafruit LSM303DLHC Triple-axis Accelerometer+Magnetometer (Compass) [part_number="Adafruit #1120"]
  Part4 = MPL3115A2 I2C Barometric Pressure, Altitude, Temperature Sensor
  LED1 = RGB LED - (4 legs) [package="5 mm [THT]"]
  R2 = Resistor [tolerance=±5% resistance=270 package="2010 [SMD]"]
  R3 = Resistor [tolerance=±5% resistance=270 package="2010 [SMD]"]
  R1 = Resistor [tolerance=±5% resistance=270 package="2010 [SMD]"]

nets:
  N1: Part1.A2, Part2.C, R3.Pin_0
  N2: Part1.A1, Part2.B, R2.Pin_0
  N3: Part1.A0, Part2.A, R1.Pin_0
  GND: Part1.GND, Part2.GND, Part3.GND, Part4.GND, LED1.green_cathode
  VIN: Part1.+3V3, Part2.3V, Part3.VIN, Part4.VIN
  N4: Part1.3, Part2.SCL, Part3.SCL, Part4.SCL
  N5: Part1.2, Part2.SDA, Part3.SDA, Part4.SDA
  N6: LED1.red_cathode, R1.Pin_1
  N7: LED1.common_anode, R2.Pin_1
  N8: LED1.blue_cathode, R3.Pin_1

custom parts:
  Adafruit Feather 32u4 FONA: This is the Adafruit Feather 32u4 FONA - our take on an 'all-in-one' Arduino-compatible + audio/sms/data capable cellular with built in USB and battery charging. Its an Adafruit Feather 32u4 with a FONA800 module, ready to rock! We have other boards and accessories in the Feather family, check'em out here. At the Feather 32u4's heart is at ATmega32u4 clocked at 8 MHz and at 3.3V logic, a chip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
  Adafruit GPS FeatherWing: Give your Feather a sense of place, with an Ultimate GPS FeatherWing. In 2013 we designed the Ultimate GPS module to satisfy all your GPS desires - and now we have brought its power and versatility plus more to our Feather series with the Adafruit Ultimate GPS FeatherWing! This FeatherWing plugs right into your Feather board and gives it a precise, sensitive, and low power GPS module for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
  Adafruit LSM303DLHC Triple-axis Accelerometer+Magnetometer (Compass): He told you "Go West, young maker!" - but you don't know which way is West! Ah, if only you had this triple-axis accelerometer/magnetometer compass module. Inside are two sensors, one is a classic 3-axis accelerometer, which can tell you which direction is down towards the Earth (by measuring gravity). The other is a magnetometer that can sense where the strongest magnetic force is coming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
  MPL3115A2 I2C Barometric Pressure, Altitude, Temperature Sensor: This pressure sensor from Freescale is a great low-cost sensing solution for precision measurement of barometric pressure and altitude. The MPL3115A2 has a typical 1.5 Pascal resolution, which can resolve altitude at 0.3 meters (compare to the BMP180 which can do 0.17m). It has some upsides compared to the BMP180, such as interrupt outputs for ultra-low power usage, and its also a heck of a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
